// Digital circuit gaming alu.dig as structural Verilog
module gaming_alu (
  input  [7:0] A,
  input  [7:0] B,
  input  [3:0] S,
  input  M,
  input  Cin,
  input  CF,
  output [7:0] Out,
  output Cout,
  output A_eq_B
);

  wire _74181_1_pin7, A_B, and_1_out, and_2_out, Arith, Cin_t, Condition, Condition_AND, Condition_OR,
       driver_12_out, multiplexer_1_out, not_2_out, or_1_out, Shift_Left, Shift_RIght, Sign, undriven,
       undriven_2, undriven_3, xnor_1_out;
  wire [0:0] multiplexer_6_out, rom_1_d;
  wire [7:0] _74181_2_pin9, multiplexer_2_out, multiplexer_3_out;
  wire [7:7] multiplexer_4_out, multiplexer_5_out;

  not not_1 (Cin_t, Cin);
  _74181 _74181_1 (
    .pin1(B[4]), .pin2(A[4]), .pin3(S[3]), .pin4(S[2]), .pin5(S[1]), .pin6(S[0]), .pin7(_74181_1_pin7),
    .pin8(M), .pin9(_74181_2_pin9[4]), .pin10(_74181_2_pin9[5]), .pin11(_74181_2_pin9[6]), .pin12(1'b0));  // open: pin13, pin14, pin15, pin16, pin17, pin18, pin19, pin20, pin21, pin22, pin23, pin24
  _74181 _74181_2 (
    .pin1(B[0]), .pin2(A[0]), .pin3(S[3]), .pin4(S[2]), .pin5(S[1]), .pin6(S[0]), .pin7(Cin), .pin8(M),
    .pin9(_74181_2_pin9[0]), .pin10(_74181_2_pin9[1]), .pin11(_74181_2_pin9[2]), .pin12(1'b0));  // open: pin13, pin14, pin15, pin16, pin17, pin18, pin19, pin20, pin21, pin22, pin23, pin24
  Multiplexer multiplexer_1 (.sel(A_B), .in_0(A[0]), .in_1(B[0]), .out(multiplexer_1_out));
  Multiplexer #(.Bits(8)) multiplexer_2 (.sel(A_B), .in_0(A), .in_1(B), .out(multiplexer_2_out));
  Multiplexer #(.Bits(8)) multiplexer_3 (.sel(A_B), .in_0(A), .in_1(B), .out(multiplexer_3_out));
  xnor xnor_1 (xnor_1_out, multiplexer_1_out, CF);
  and and_1 (and_1_out, multiplexer_1_out, CF);
  or or_1 (or_1_out, multiplexer_1_out, CF);
  and and_2 (and_2_out, undriven, undriven_2);
  ROM #(.AddrBits(5), .Bits(9)) rom_1 (
    .A({M, S}), .sel(1'b1),
    .D({A_B, Condition_OR, Condition_AND, Condition, Arith, Shift_RIght, Shift_Left, Sign, rom_1_d[0]}));
  Multiplexer multiplexer_4 (.sel(A_B), .in_0(A[7]), .in_1(B[7]), .out(multiplexer_4_out[7]));
  Multiplexer multiplexer_5 (.sel(Arith), .in_0(Cin_t), .in_1(multiplexer_3_out[7]), .out(multiplexer_5_out[7]));
  Multiplexer #(.Selector_Bits(2)) multiplexer_6 (
    .sel({Condition_AND, Condition_OR}), .in_0(CF), .in_1(or_1_out), .in_2(and_1_out), .in_3(or_1_out),
    .out(multiplexer_6_out[0]));
  assign A_eq_B = rom_1_d[0] ? and_2_out : 1'bz;  // Driver driver_1
  assign Out = rom_1_d[0] ? _74181_2_pin9 : 8'bz;  // Driver driver_2
  assign A_eq_B = Sign ? 1'b0 : 1'bz;  // Driver driver_3
  assign Out = Sign ? {8{multiplexer_4_out[7]}} : 8'bz;  // Driver driver_4
  assign A_eq_B = Shift_Left ? 1'b0 : 1'bz;  // Driver driver_5
  assign Out = Shift_Left ? {multiplexer_2_out[6:0], Cin_t} : 8'bz;  // Driver driver_6
  assign A_eq_B = Shift_RIght ? 1'b0 : 1'bz;  // Driver driver_7
  assign Out = Shift_RIght ? {multiplexer_5_out[7], multiplexer_3_out[7:1]} : 8'bz;  // Driver driver_8
  assign A_eq_B = Condition ? xnor_1_out : 1'bz;  // Driver driver_9
  assign Out = Condition ? {{7{1'b0}}, multiplexer_6_out[0]} : 8'bz;  // Driver driver_10
  assign Cout = rom_1_d[0] ? undriven_3 : 1'bz;  // Driver driver_11
  assign Cout = ~rom_1_d[0] ? not_2_out : 1'bz;  // DriverInvSel driverinvsel_1
  not not_2 (not_2_out, driver_12_out);
  assign driver_12_out = Sign ? 1'b0 : 1'bz;  // Driver driver_12
  assign driver_12_out = Shift_Left ? multiplexer_2_out[7] : 1'bz;  // Driver driver_13
  assign driver_12_out = Shift_RIght ? multiplexer_3_out[0] : 1'bz;  // Driver driver_14
  assign driver_12_out = Condition ? multiplexer_6_out[0] : 1'bz;  // Driver driver_15

  // Notes on the sheet:
  //   contents of rom_1 (hex, n*v repeats v):
  //   1,8,108,1,18,118,1,4,104,1,2,102,20,60,160,1,1,a0,1a0,1,1,1,1,1,1,1,1,1,1,1,1,1
endmodule
