// Digital circuit gaming cache.dig as structural Verilog
module gaming_cache (
  input  [15:0] A,
  input  str,
  input  ld,
  input  C,
  input  mready,
  output [7:0] Dbus,
  output [7:0] Dram,
  output sr,
  output lr,
  output [15:0] Aram,
  output ready
);

  wire and_2_out, and_3_out, and_4_out, and_5_out, and_6_out, and_7_out, and_8_out, and_9_out, and_10_out,
       and_11_out, and_12_out, block_index_ovf, Cache_Select, comparator_1_eq, not_1_out, not_2_out,
       not_3_out, or_1_out, or_2_out, or_3_out, RAM_Driver_Read, undriven, undriven_3, undriven_4,
       undriven_5, undriven_6, undriven_7, undriven_8, undriven_9;
  wire [5:0] multiplexer_2_out, tag_valid_2_q, tag_valid_3_q;
  wire [5:5] multiplexer_1_out;
  wire [7:0] demultiplexer_1_out_0, demultiplexer_1_out_1, Main_Cache_D, Stack_Cache_D;
  wire [8:0] undriven_2;
  wire [13:6] tag_q;

  and and_1 (Cache_Select, A[9], A[10], A[11], A[12], A[13], A[14], A[15]);
  Register #(.Bits(15)) tag_valid ();  // open: D, C, en, Q
  RAMDualPort #(.Bits(8)) block ();  // open: A, Din, str, C, ld, D
  Counter #(.Bits(2)) block_index (.C(undriven), .out(Aram[1:0]), .ovf(block_index_ovf));  // open: en, clr
  Register #(.Bits(14)) tag (.C(undriven), .Q({tag_q, Aram[7:2]}));  // open: D, en
  Demultiplexer #(.Bits(8)) demultiplexer_1 (
    .sel(Cache_Select), .in(Dram), .out_0(demultiplexer_1_out_0), .out_1(demultiplexer_1_out_1));
  not not_1 (not_1_out, Cache_Select);
  Multiplexer multiplexer_1 (
    .sel(and_7_out), .in_0(multiplexer_2_out[5]), .in_1(undriven_3), .out(multiplexer_1_out[5]));
  assign Main_Cache_D = and_3_out ? demultiplexer_1_out_0 : 8'bz;  // Driver driver_1
  assign Stack_Cache_D = and_2_out ? demultiplexer_1_out_1 : 8'bz;  // Driver driver_2
  and and_2 (and_2_out, Cache_Select, and_4_out);
  and and_3 (and_3_out, not_1_out, and_4_out);
  and and_4 (and_4_out, RAM_Driver_Read, mready);
  and and_5 (and_5_out, and_7_out, undriven_2[3]);
  not not_2 (not_2_out, undriven_2[3]);
  and and_6 (and_6_out, and_7_out, not_2_out);
  Register #(.Bits(6)) tag_valid_2 (
    .D({multiplexer_1_out[5], undriven_2[8:4]}), .C(undriven_4), .en(and_5_out), .Q(tag_valid_2_q));
  Register #(.Bits(6)) tag_valid_3 (
    .D({multiplexer_1_out[5], undriven_2[8:4]}), .C(undriven_4), .en(and_6_out), .Q(tag_valid_3_q));
  Comparator #(.Bits(5)) comparator_1 (
    .a(undriven_2[8:4]), .b(multiplexer_2_out[4:0]), .eq(comparator_1_eq));  // open: gt, lt
  Multiplexer #(.Bits(6)) multiplexer_2 (
    .sel(not_2_out), .in_0(tag_valid_2_q), .in_1(tag_valid_3_q), .out(multiplexer_2_out));
  and and_7 (and_7_out, or_1_out, or_2_out);
  or or_1 (or_1_out, comparator_1_eq, undriven_5);
  not not_3 (not_3_out, undriven_2[3]);
  and and_8 (and_8_out, or_1_out, or_3_out);
  or or_2 (or_2_out, undriven_6, undriven_7);
  and and_9 (and_9_out, and_7_out, undriven_2[3]);
  and and_10 (and_10_out, and_8_out, undriven_2[3]);
  and and_11 (and_11_out, and_7_out, not_3_out);
  and and_12 (and_12_out, and_8_out, not_3_out);
  or or_3 (or_3_out, undriven_8, undriven_9);
  RAMSinglePort #(.AddrBits(3), .Bits(8)) block_2 (
    .A(undriven_2[2:0]), .str(and_9_out), .C(undriven_4), .ld(and_10_out), .D(Stack_Cache_D));
  RAMSinglePort #(.AddrBits(3), .Bits(8)) block_3 (
    .A(undriven_2[2:0]), .str(and_11_out), .C(undriven_4), .ld(and_12_out), .D(Stack_Cache_D));
  // Pins of 8 and 16 bits meet at Aram

  // Other names for the same wires on the sheet: Clock = C

  // Notes on the sheet:
  //   A: Address
  //   str: Store
  //   ld: Load
  //   Dbus: Bidirectional data
  //   Main Cache
  //   128 bytes, 4 byte blocks
  //   2-way set associative
  //   Main Block
  //   Stack Cache
  //   (upper 512)
  //   16 bytes, 8 byte blocks
  //   Direct mapped
  //   A
  //   dirty
  //   (in)
  //   RAM Driver
  //   Stack Cache
  //   dirty
  //   hit
  //   str
  //   ld
  //   C
  //   D
endmodule
