// Digital circuit gaming externals.dig as structural Verilog
module gaming_externals (
  input  Read,
  input  Write,
  input  Clock,
  output [7:0] Bus
);

  wire and_1_out, and_2_out, and_3_out, and_4_out, EEPROM_Enable, KBT_Enable, t_ff_1_nq;
  wire [7:0] register_1_q;
  wire [15:0] keyboard_1_d;

  and and_1 (and_1_out, Clock, 1'b0);
  T_FF t_ff_1 (.T(and_1_out), .C(and_1_out), .nQ(t_ff_1_nq));  // open: Q
  and and_2 (and_2_out, t_ff_1_nq, Write);
  Register #(.Bits(8)) register_1 (.D(Bus), .C(and_1_out), .en(and_2_out), .Q(register_1_q));
  Decoder decoder_1 (.sel(register_1_q[0]), .out_0(KBT_Enable), .out_1(EEPROM_Enable));
  and and_3 (and_3_out, Write, KBT_Enable);
  and and_4 (and_4_out, Read, KBT_Enable);
  Terminal terminal_1 (.D(Bus[6:0]), .C(Clock), .en(and_3_out));
  Keyboard keyboard_1 (.C(Clock), .en(and_4_out), .D(keyboard_1_d));  // open: av
  assign Bus = Read ? keyboard_1_d[7:0] : 8'bz;  // Driver driver_1

  // Other names for the same wires on the sheet: IO_Read = Read; IO_Write = Write
endmodule
