// Digital circuit gaming ram.dig as structural Verilog
module gaming_ram (
  input  [15:0] A,
  input  ld,
  input  str,
  input  C,
  output [7:0] D,
  output r
);

  wire and_1_out, and_2_out, and_3_out, not_1_out;

  and and_1 (and_1_out, A[15], str);
  and and_2 (and_2_out, A[15], ld);
  not not_1 (not_1_out, A[15]);
  and and_3 (and_3_out, not_1_out, ld);
  RAMSinglePort #(.AddrBits(15), .Bits(8)) _32kx8_RAM (.A(A[14:0]), .str(and_1_out), .C(C), .ld(and_2_out), .D(D));
  ROM #(.AddrBits(15), .isProgramMemory("true"), .Bits(8)) _32kx8_ROM (.A(A[14:0]), .sel(and_3_out), .D(D));

  assign r = 1'b1;

  // Notes on the sheet:
  //   A: Address In
  //   r: ready
  //   contents of _32kx8_ROM (hex, n*v repeats v):
  //   2,0,1,ad,3d,0,ad,3d,0,2,2,3,ad,3d,0,ad,3d,0,2,4,5,ad,3d,0,ad,3d,0,2,6,7,ad,3d,0,ad,
  //   3d,0,2,8,9,ad,3d,0,ad,3d,0,fd,a,2,1,0,ad,3d,0,ad,3d,0,fd,a,a7,0,0,b0,0,2f,2,c2,30,
  //   fb,ae,0,0,0,0,0,0,0,0,0,0,0,0,0,0,0,0,0,0,0,0,0,0,0,0,0,0,0,0,0,0,0,0,0,0,0,0,0,0,
  //   0,0,0,0,0,0,0,0,0,0,0,0,0,0,0,0,0,0,0,0,0,0,0,0,0,0,0,0,0,0,0,0,0,0,0,0,0,0,0,0,0,
  //   0,0,0,0,0,0,0,0,0,0,0,0,0,0,0,0,0,0,0,0,0,0,0,0,0,0,0,0,0,0,0,0,0,0,0,0,0,0,0,0,0,
  //   0,0,0,0,0,0,0,0,0,0,0,0,0,0,0,0,0,0,0,0,0,0,0,0,0,0,0,0,0,0,0,0,0,0,0,0,0,0,0,0,0,
  //   7a,79,78,77,76,75,74,73,72,71,70,6f,6e,6d,6c,6b,6a,69,68,67,66,65,64,63,62,61,20,
  //   61,62,63,64,65,66,67,68,69,6a,6b,6c,6d,6e,6f,70,71,72,43,74,75,76,77,78,79,7a
endmodule
