// Digital circuit gaming alu.dig as structural Verilog
module gaming_alu (
  input  [7:0] A,
  input  [7:0] B,
  input  [3:0] S,
  input  M,
  input  Cin,
  output [7:0] Out,
  output Cout,
  output A_eq_B
);

  wire _74181_1_pin7, undriven, undriven_2;

  _74181 _74181_1 (
    .pin1(B[4]), .pin2(A[4]), .pin3(S[3]), .pin4(S[2]), .pin5(S[1]), .pin6(S[0]), .pin7(_74181_1_pin7),
    .pin8(M), .pin9(Out[4]), .pin10(Out[5]), .pin11(Out[6]), .pin12(1'b0));  // open: pin13, pin14, pin15, pin16, pin17, pin18, pin19, pin20, pin21, pin22, pin23, pin24
  _74181 _74181_2 (
    .pin1(B[0]), .pin2(A[0]), .pin3(S[3]), .pin4(S[2]), .pin5(S[1]), .pin6(S[0]), .pin7(Cin), .pin8(M),
    .pin9(Out[0]), .pin10(Out[1]), .pin11(Out[2]), .pin12(1'b0));  // open: pin13, pin14, pin15, pin16, pin17, pin18, pin19, pin20, pin21, pin22, pin23, pin24
  and and_1 (A_eq_B, undriven, undriven_2);
endmodule
