// Digital circuit gaming pc.dig as structural Verilog
module gaming_pc (
  input  clk
);

  wire Address_Bus_Enable, AHS_SPW, ALU_Enable, and_1_out, and_2_out, and_3_out, and_4_out, and_5_out,
       and_6_out, BP_Enable, Bus_Enable, Carry, Carry_Flag_q, Carry_Write, CF_Select, Cin_Select,
       Comparator_Invert, Comparator_Select, Condition_Enable, Condition_Flag_q, Condition_Out,
       Condition_Write, d_ff_1_nq, gaming_alu_1_a_eq_b, gaming_alu_1_cout, IO_Read, IO_Write, IP_Conditional,
       IP_Enable, IP_Write, M, Memory_Load, Memory_Store, multiplexer_3_out, multiplexer_4_out,
       multiplexer_5_out, Next_Instruction, not_1_out, or_1_out, or_2_out, Reg_A_Read, Reg_A_Write,
       Reg_B_Read, Reg_B_Write, S0, S1, S2, S3, SP_Direction, SP_Enable, xor_1_out;
  wire [1:0] Address_Select, Bus_Select;
  wire [3:0] Stage_Counter_out;
  wire [6:0] driver_3_out;
  wire [7:0] A, B, driver_1_out, driver_2_out, gaming_alu_1_out, Instruction_q, keyboard_1_d,
       multiplexer_2_out;
  wire [7:7] driver_3_out_2;
  wire [15:0] BP, IP_out, multiplexer_1_out, Stack_Pointer_out;
  wire [15:8] keyboard_1_d_2;

  D_FF d_ff_1 (.D(1'b1), .C(clk), .nQ(d_ff_1_nq));  // open: Q
  or or_1 (or_1_out, IP_Write, Condition_Out);
  or or_2 (or_2_out, d_ff_1_nq, SP_Enable);
  and and_1 (and_1_out, SP_Enable, AHS_SPW);
  Register #(.Bits(8)) Register_A (.D({driver_3_out_2[7], driver_3_out}), .C(clk), .en(Reg_A_Write), .Q(A));
  Register #(.Bits(8)) Register_B (.D({driver_3_out_2[7], driver_3_out}), .C(clk), .en(Reg_B_Write), .Q(B));
  Register #(.Bits(16)) Base_Pointer (.D(multiplexer_1_out), .C(clk), .en(BP_Enable), .Q(BP));
  CounterPreset #(.Bits(16)) Stack_Pointer (
    .en(or_2_out), .C(clk), .dir(~SP_Direction), .in(multiplexer_1_out), .ld(and_1_out), .clr(1'b0),
    .out(Stack_Pointer_out));  // open: ovf
  CounterPreset #(.Bits(16)) IP (
    .en(IP_Enable), .C(clk), .dir(1'b0), .in(multiplexer_1_out), .ld(or_1_out), .clr(1'b0), .out(IP_out));  // open: ovf
  Register #(.Bits(8)) Instruction (
    .D({driver_3_out_2[7], driver_3_out}), .C(clk), .en(Next_Instruction), .Q(Instruction_q));
  Counter #(.Bits(4)) Stage_Counter (.en(1'b1), .C(clk), .clr(Next_Instruction), .out(Stage_Counter_out));  // open: ovf
  // Probe SP on Stack_Pointer_out
  // Probe IP on IP_out
  // Probe Instruction on Instruction_q
  // Probe Stage on Stage_Counter_out
  assign driver_1_out = Reg_A_Read ? A : 8'bz;  // Driver driver_1
  assign driver_2_out = Reg_B_Read ? B : 8'bz;  // Driver driver_2
  Multiplexer #(.Selector_Bits(2), .Bits(16)) multiplexer_1 (
    .sel(Address_Select), .in_0({A, B}), .in_1(BP), .in_2(Stack_Pointer_out), .in_3(IP_out),
    .out(multiplexer_1_out));
  ROM #(.AddrBits(12), .Bits(32)) Control_ROM (
    .A({Instruction_q, Stage_Counter_out}), .sel(1'b1),
    .D({IO_Write, Condition_Enable, Condition_Write, Comparator_Invert, Comparator_Select, Carry_Write, Cin_Select, CF_Select, Carry, M, S3, S2, S1, S0, Next_Instruction, IP_Enable, IP_Write, IP_Conditional, SP_Enable, SP_Direction, BP_Enable, Reg_B_Read, Reg_B_Write, Reg_A_Read, Reg_A_Write, Memory_Store, AHS_SPW, Bus_Enable, Bus_Select, Address_Select}));
  Multiplexer #(.Bits(8)) multiplexer_2 (
    .sel(AHS_SPW), .in_0(multiplexer_1_out[7:0]), .in_1(multiplexer_1_out[15:8]), .out(multiplexer_2_out));
  // Probe Address on multiplexer_1_out
  // Probe BP on BP
  assign {driver_3_out_2[7], driver_3_out} = Address_Bus_Enable ? multiplexer_2_out : 8'bz;  // Driver driver_3
  and and_2 (and_2_out, multiplexer_1_out[15], Memory_Store);
  and and_3 (and_3_out, multiplexer_1_out[15], Memory_Load);
  not not_1 (not_1_out, multiplexer_1_out[15]);
  and and_4 (and_4_out, not_1_out, Memory_Load);
  // Probe Bus on {driver_3_out_2[7], driver_3_out}
  // Probe A on A
  // Probe B on B
  RAMSinglePort #(.AddrBits(15), .Bits(8)) _32kx8_RAM (
    .A(multiplexer_1_out[14:0]), .str(and_2_out), .C(clk), .ld(and_3_out),
    .D({driver_3_out_2[7], driver_3_out}));
  ROM #(.AddrBits(15), .isProgramMemory("true"), .Bits(8)) _32kx8_ROM (
    .A(multiplexer_1_out[14:0]), .sel(and_4_out), .D({driver_3_out_2[7], driver_3_out}));
  Terminal terminal_1 (.D(driver_3_out), .C(clk), .en(IO_Write));
  assign {driver_3_out_2[7], driver_3_out} = IO_Read ? keyboard_1_d : 8'bz;  // Driver driver_4
  Keyboard keyboard_1 (.C(clk), .en(IO_Read), .D({keyboard_1_d_2, keyboard_1_d}));  // open: av
  Demultiplexer #(.Selector_Bits(2)) demultiplexer_1 (
    .sel(Bus_Select), .in(Bus_Enable), .out_0(Memory_Load), .out_1(ALU_Enable), .out_2(Address_Bus_Enable),
    .out_3(IO_Read));
  and and_5 (and_5_out, clk, Carry_Write);
  Multiplexer multiplexer_3 (.sel(Cin_Select), .in_0(Carry_Flag_q), .in_1(Carry), .out(multiplexer_3_out));
  D_FF Carry_Flag (.D(multiplexer_4_out), .C(and_5_out), .Q(Carry_Flag_q));  // open: nQ
  gaming_alu gaming_alu_1 (
    .A(driver_1_out), .B(driver_2_out), .S({S3, S2, S1, S0}), .M(M), .Cin(multiplexer_3_out),
    .Out(gaming_alu_1_out), .Cout(gaming_alu_1_cout), .A_eq_B(gaming_alu_1_a_eq_b));
  Multiplexer multiplexer_4 (.sel(CF_Select), .in_0(gaming_alu_1_cout), .in_1(Carry), .out(multiplexer_4_out));
  Multiplexer multiplexer_5 (
    .sel(Comparator_Select), .in_0(gaming_alu_1_cout), .in_1(gaming_alu_1_a_eq_b), .out(multiplexer_5_out));
  assign {driver_3_out_2[7], driver_3_out} = ALU_Enable ? gaming_alu_1_out : 8'bz;  // Driver driver_5
  xor xor_1 (xor_1_out, multiplexer_5_out, Comparator_Invert);
  D_FF Condition_Flag (.D(xor_1_out), .C(and_6_out), .Q(Condition_Flag_q));  // open: nQ
  and and_6 (and_6_out, clk, Condition_Write);
  and and_7 (Condition_Out, Condition_Flag_q, Condition_Enable);

  // Other names for the same wires on the sheet: Clock = clk

  // Notes on the sheet:
  //   clk: Hz: 2
  //   contents of Control_ROM (hex, n*v repeats v):
  //   30013,0,0,0,0,0,0,0,0,0,0,0,0,0,0,0,33013,0,0,0,0,0,0,0,0,0,0,0,0,0,0,0,9a,10213,
  //   6a40714,ba,194,2020,30013,0,0,0,0,0,0,0,0,0,0,0,0,0,0,0,0,0,0,0,0,0,0,0,0,0,12093,
  //   2800156,30013,0,0,0,0,0,0,0,0,0,0,0,0,0,0,0,0,0,0,0,0,0,0,0,0,0,0,0,0,0,0,0,0,0,0,
  //   0,0,0,0,0,0,0,0,0,0,0,0,0,0,0,0,0,0,0,0,0,0,0,0,0,0,0,0,0,0,0,0,0,0,0,0,0,0,0,0,0,
  //   0,0,0,0,0,0,0,0,0,0,0,0,0,0,0,0,0,0,0,0,0,0,0,0,0,0,0,0,0,0,0,0,0,0,0,0,0,0,0,0,0,
  //   0,0,0,0,0,0,0,0,0,0,0,0,0,0,0,0,0,0,0,0,0,0,0,0,0,0,0,0,0,0,0,0,0,0,0,0,0,0,0,0,0,
  //   0,0,0,0,0,0,0,0,0,0,0,0,0,0,0,0,0,0,0,0,0,0,0,0,0,0,0,0,0,0,0,0,0,0,0,0,0,0,0,0,0,
  //   0,0,0,0,0,0,0,0,0,0,0,0,0,0,0,0,0,0,0,0,0,0,0,0,0,0,0,0,0,0,0,0,0,0,0,0,0,0,0,0,0,
  //   0,0,0,0,0,0,0,0,0,0,0,0,0,0,0,0,0,0,0,0,0,0,0,0,0,0,0,0,0,0,0,0,0,0,0,0,0,0,0,0,0,
  //   0,0,0,0,0,0,0,0,0,0,0,0,0,0,0,0,0,0,0,0,0,0,0,0,0,0,0,0,0,0,0,0,0,0,0,0,0,0,0,0,0,
  //   0,0,0,0,0,0,0,0,0,0,0,0,0,0,0,0,0,0,0,0,0,0,0,0,0,0,0,0,0,0,0,0,0,0,0,0,0,0,0,0,0,
  //   0,0,0,0,0,0,0,0,0,0,0,0,0,0,0,0,0,0,0,0,0,0,0,0,0,0,0,0,0,0,0,0,0,0,0,0,0,0,0,0,0,
  //   0,0,0,0,0,0,0,0,0,0,0,0,0,0,0,0,0,0,0,0,0,0,0,0,0,0,0,0,0,0,0,0,0,0,0,0,0,0,0,0,0,
  //   0,0,0,0,0,0,0,0,0,0,0,0,0,0,0,0,0,0,0,0,0,0,0,0,0,0,0,0,0,0,0,0,0,0,0,0,0,0,0,0,0,
  //   0,0,0,0,0,0,0,0,0,0,0,0,0,0,0,0,0,0,0,0,0,0,0,0,0,0,0,0,0,0,0,0,0,0,0,0,0,0,0,0,0,
  //   0,0,0,0,0,0,0,0,0,0,0,0,0,0,0,0,0,0,0,0,0,0,0,0,0,0,0,0,0,0,0,0,0,0,0,0,0,0,0,0,0,
  //   0,0,0,0,0,0,0,0,0,0,0,0,0,0,0,0,0,0,0,0,0,0,0,0,0,0,0,0,0,0,0,0,0,0,0,0,0,0,0,0,0,
  //   0,0,0,0,0,0,0,0,0,0,0,0,0,0,0,0,0,0,0,0,0,0,0,0,0,0,0,0,0,0,0,0,0,0,0,0,0,0,0,0,0,
  //   0,0,0,0,0,0,0,0,0,0,0,0,0,0,0,0,0,0,0,0,0,0,0,0,0,0,0,0,0,0,0,0,0,0,0,0,0,0,0,0,0,
  //   0,0,0,0,0,0,0,0,0,0,0,0,0,0,0,0,0,0,0,0,0,0,0,0,0,0,0,0,0,0,0,0,0,0,0,0,0,0,0,0,0,
  //   0,0,0,0,0,0,0,0,0,0,0,0,0,0,0,0,0,0,0,0,0,0,0,0,0,0,0,0,0,0,0,0,0,0,0,0,0,0,0,0,0,
  //   0,0,0,0,0,0,0,0,0,0,0,0,0,0,0,0,0,0,0,0,0,0,0,0,0,0,0,0,0,0,0,0,0,0,0,0,0,0,0,0,0,
  //   0,0,0,0,0,0,0,0,0,0,0,0,0,0,0,0,0,0,0,0,0,0,0,0,0,0,0,0,0,0,0,0,0,0,0,0,0,0,0,0,0,
  //   0,0,0,0,0,0,0,0,0,0,0,0,0,0,0,0,0,0,0,0,0,0,0,0,0,0,0,0,0,0,0,0,0,0,0,0,0,0,0,0,0,
  //   0,0,0,0,0,0,0,0,0,0,0,0,0,0,0,0,0,0,0,0,0,0,0,0,0,0,0,0,0,0,0,0,0,0,0,0,0,0,0,0,0,
  //   0,0,0,0,0,0,0,0,0,0,0,0,0,0,0,0,0,0,0,0,0,0,0,0,0,0,0,0,0,0,0,0,0,0,0,0,0,0,0,0,0,
  //   0,0,0,0,0,0,0,0,0,0,0,0,0,0,0,0,0,0,0,0,0,0,0,0,0,0,0,0,0,0,0,0,0,0,0,0,0,0,0,0,0,
  //   0,0,0,0,0,0,0,0,0,0,0,0,0,0,0,0,0,0,0,0,0,0,0,0,0,0,0,0,0,0,0,0,0,0,0,0,0,0,0,0,0,
  //   0,0,0,0,0,0,0,0,0,0,0,0,0,0,0,0,0,0,0,0,0,0,0,0,0,0,0,0,0,0,0,0,0,0,0,0,0,0,0,0,0,
  //   0,0,0,0,0,0,0,0,0,0,0,0,0,0,0,0,0,0,0,0,0,0,0,0,0,0,0,0,0,0,0,0,0,0,0,0,0,0,0,0,0,
  //   0,0,0,0,0,0,0,0,0,0,0,0,0,0,0,0,0,0,0,0,0,0,0,0,0,0,0,0,0,0,0,0,0,0,0,0,0,0,0,0,0,
  //   0,0,0,0,0,0,0,0,0,0,0,0,0,0,0,0,0,0,0,0,0,0,0,0,0,0,0,0,0,0,0,0,0,0,0,0,0,0,0,0,0,
  //   0,0,0,0,0,0,0,0,0,0,0,0,0,0,0,0,0,0,0,0,0,0,0,0,0,0,0,0,0,0,0,0,0,0,0,0,0,0,0,0,0,
  //   0,0,0,0,0,0,0,0,0,0,0,0,0,0,0,0,0,0,0,0,0,0,0,0,0,0,0,0,0,0,0,0,0,0,0,0,0,0,0,0,0,
  //   0,0,0,0,0,0,0,0,0,0,0,0,0,0,0,0,0,0,0,0,0,0,0,0,0,0,0,0,0,0,0,0,0,0,0,0,0,0,0,0,0,
  //   0,0,0,0,0,0,0,0,0,0,0,0,0,0,0,0,0,0,0,0,0,0,0,0,0,0,0,0,0,0,0,0,0,0,0,0,0,0,0,0,0,
  //   0,0,0,0,0,0,0,0,0,0,0,0,0,0,0,0,0,0,0,0,0,0,0,0,0,0,0,0,0,0,0,0,0,0,0,0,0,0,0,0,0,
  //   0,0,0,0,0,0,0,0,0,0,0,0,0,0,0,0,0,0,0,0,0,0,0,0,0,0,0,0,0,0,0,0,0,0,0,0,0,0,0,0,0,
  //   0,0,0,0,0,0,0,0,0,0,0,0,0,0,0,0,0,0,0,0,0,0,0,0,0,0,0,0,0,0,0,0,0,0,0,0,0,0,0,0,0,
  //   0,0,0,0,0,0,0,0,0,0,0,0,0,0,0,0,0,0,0,0,0,0,0,0,0,0,0,0,0,0,0,0,0,0,0,0,0,0,0,0,0,
  //   0,0,0,0,0,0,0,0,0,0,0,0,0,0,0,0,0,0,0,0,0,0,0,0,0,0,0,0,0,0,0,0,0,0,0,0,0,0,0,0,0,
  //   0,0,0,0,0,0,0,0,0,0,0,0,0,0,0,0,0,0,0,0,0,0,0,0,0,0,0,0,0,0,0,0,0,0,0,0,0,0,0,0,0,
  //   0,0,0,0,0,0,0,0,0,0,0,0,0,0,0,0,0,0,0,0,0,0,0,0,0,0,0,0,0,0,0,0,0,0,0,0,0,0,0,0,0,
  //   0,0,0,0,0,0,0,0,0,0,0,0,0,0,0,0,0,0,0,0,0,0,0,0,0,0,0,0,0,0,0,0,0,0,0,0,0,0,0,0,0,
  //   0,0,0,0,0,0,0,0,0,0,0,0,0,0,0,0,0,0,0,0,0,0,0,0,0,0,0,0,0,0,0,0,0,0,0,0,0,0,0,0,0,
  //   0,0,0,0,0,0,0,0,0,0,0,0,0,0,0,0,0,0,0,0,0,0,0,0,0,0,0,0,0,0,0,0,0,0,0,0,0,0,0,0,0,
  //   0,0,0,0,0,0,0,0,0,0,0,0,0,0,0,0,0,0,0,0,0,0,0,0,0,0,0,0,0,0,0,0,0,0,0,0,0,0,0,0,0,
  //   0,0,0,0,0,0,0,0,0,0,0,0,0,0,0,0,0,0,0,0,0,0,0,0,0,0,0,0,0,0,0,0,0,0,0,0,0,0,0,0,0,
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  //   contents of _32kx8_ROM (hex, n*v repeats v):
  //   0,0,0,0,0,0,0,0,0,0,0,0,0,0,0,0,0,0,0,0,0,0,0,0,0,0,0,0,0,0,0,0,fe,fe,fe,fe,fe,fe,
  //   fe,fe,fe,fe,fe,fe,fe,fe,fe,fe,2,8,ff,ff,ff,ff,ff,ff,ff,ff
endmodule
